# Fritzing sketch fritzing1 (saved by Fritzing 0.9.9b)

parts:
  Part1 = Breakout Board for Electret Microphone
  Part2 = Arduino Uno (Rev3) - ICSP
  LED1 = LEDs [package=led10mm]

nets:
  VCC: Part1.VCC, Part2.5V
  GND: Part1.GND, Part2.GND, LED1.C
  N1: Part1.AUD, Part2.D2
  N2: Part2.D3_PWM, LED1.A
